// Logisim project DSDLAB3 (1).circ as structural Verilog: 2 circuits, main circuit LAB3
module LAB3 (
  input  A1,
  input  A0,
  input  B1,
  input  B0,
  output C1,
  output C0
);

  wire and_1_out, and_2_out, and_3_out, and_4_out, not_1_out, not_2_out;

  or or_1 (C1, B1, A1);
  not not_1 (not_1_out, A1);
  and and_1 (and_1_out, not_1_out, B0);
  and and_2 (and_2_out, B1, B0);
  and and_3 (and_3_out, A0, not_2_out);
  not not_2 (not_2_out, B1);
  and and_4 (and_4_out, A1, A0);
  or or_2 (C0, and_1_out, and_2_out, and_3_out, and_4_out);

  // Notes on the sheet:
  //   A1'*B0
  //   B1*B0
  //   A0*B1'
  //   A1*A0
  //   A1+B1
  //   (A1*B0)+(B1*B0)+(A0*B1')+(A1*A0)
endmodule

module TEST (
  input  in_1,
  input  in_2,
  input  in_3,
  input  in_4,
  input  in_5,
  input  in_6,
  input  in_7,
  input  in_8,
  input  in_9,
  input  in_10,
  input  in_11,
  input  in_12,
  input  in_13,
  input  in_14,
  input  in_15,
  input  in_16,
  input  in_17,
  input  in_18,
  input  in_19,
  input  in_20,
  input  in_21,
  input  in_22,
  input  in_23,
  input  in_24,
  input  in_25,
  input  in_26,
  input  in_27,
  input  in_28,
  input  in_29,
  input  in_30,
  input  in_31,
  input  in_32
);

  Multiplexer #(.select(4)) multiplexer_1 (
    .in4(in_6), .in5(in_7));  // open: in0, in1, in2, in3, in6, in7, in8, in9, in10, in11, in12, in13, in14, in15, out, sel, en
  Multiplexer #(.select(4)) multiplexer_2 ();  // open: in0, in1, in2, in3, in4, in5, in6, in7, in8, in9, in10, in11, in12, in13, in14, in15, out, sel, en
endmodule
