// Logisim project DSDLAB3.circ as structural Verilog: 1 circuit, main circuit LAB3
module LAB3 (
  input  A1,
  input  A0,
  input  B1,
  input  B0,
  output C1,
  output C0
);

  wire and_1_out, and_2_out, and_3_out, and_4_out, not_1_out, not_2_out;

  or or_1 (C1, B1, A1);
  not not_1 (not_1_out, A1);
  and and_1 (and_1_out, not_1_out, B0);
  and and_2 (and_2_out, B1, B0);
  and and_3 (and_3_out, A0, not_2_out);
  not not_2 (not_2_out, B1);
  and and_4 (and_4_out, A1, A0);
  or or_2 (C0, and_1_out, and_2_out, and_3_out, and_4_out);

  // Notes on the sheet:
  //   A1'*B0
  //   B1*B0
  //   A0*B1'
  //   A1*A0
  //   A1+B1
  //   (A1*B0)+(B1*B0)+(A0*B1')+(A1*A0)
endmodule
