// Logisim project DSDLAB4.circ as structural Verilog: 7 circuits, main circuit PART1
module PART1 (
  input  A1,
  input  A0,
  input  B1,
  input  B0,
  output C1,
  output C0
);

  Multiplexer #(.select(4), .enable("false")) multiplexer_1 (
    .in0(1'b0), .in1(1'b0), .in2(1'b1), .in3(1'b1), .in4(1'b0), .in5(1'b0), .in6(1'b1), .in7(1'b1),
    .in8(1'b1), .in9(1'b1), .in10(1'b1), .in11(1'b1), .in12(1'b1), .in13(1'b1), .in14(1'b1), .in15(1'b1),
    .out(C1), .sel({A1, A0, B1, B0}));
  Multiplexer #(.select(4), .enable("false")) multiplexer_2 (
    .in0(1'b0), .in1(1'b1), .in2(1'b0), .in3(1'b1), .in4(1'b1), .in5(1'b1), .in6(1'b0), .in7(1'b1),
    .in8(1'b0), .in9(1'b0), .in10(1'b0), .in11(1'b1), .in12(1'b1), .in13(1'b1), .in14(1'b1), .in15(1'b1),
    .out(C0), .sel({A1, A0, B1, B0}));
endmodule

module PART2 (
  input  A1,
  input  A0,
  input  B1,
  input  B0,
  output C1,
  output C0
);

  wire multiplexer_1_out, multiplexer_2_out, multiplexer_4_out, multiplexer_5_out;

  Multiplexer #(.enable("false")) multiplexer_1 (.in0(1'b0), .in1(1'b1), .out(multiplexer_1_out), .sel(A1));
  Multiplexer #(.enable("false")) multiplexer_2 (.in0(1'b0), .in1(1'b1), .out(multiplexer_2_out), .sel(B1));
  Multiplexer #(.enable("false")) multiplexer_3 (
    .in0(multiplexer_1_out), .in1(multiplexer_2_out), .out(C1), .sel(multiplexer_2_out));
  Multiplexer #(.enable("false")) multiplexer_4 (.in0(B0), .in1(A0), .out(multiplexer_4_out), .sel(A1));
  Multiplexer #(.enable("false")) multiplexer_5 (.in0(A0), .in1(B0), .out(multiplexer_5_out), .sel(B1));
  Multiplexer #(.enable("false")) multiplexer_6 (
    .in0(multiplexer_4_out), .in1(multiplexer_5_out), .out(C0), .sel(multiplexer_5_out));
endmodule

module NANDtemplate (
  input  in_1,
  input  in_2,
  input  in_3,
  input  in_4,
  input  in_5,
  input  in_6,
  input  in_7,
  input  in_8,
  input  in_9,
  input  in_10,
  input  in_11,
  input  in_12,
  input  in_13,
  input  in_14,
  input  in_15,
  input  in_16,
  output out_17,
  output out_18,
  output out_19,
  output out_20,
  output out_21,
  output out_22,
  output out_23,
  output out_24
);

  wire AND_3_out, AND_4_out, AND_out, OR_2_out, OR_4_out, OR_out;

  nand NAND (out_17, in_1, in_3);
  nand NOT (out_19, in_5, in_5);
  nand AND (AND_out, in_7, in_9);
  nand OR (OR_out, in_12, in_12);
  nand OR_2 (OR_2_out, in_14, in_14);
  nand AND_2 (out_21, AND_out, AND_out);
  nand OR_3 (out_23, OR_out, OR_2_out);
  nor NOR (out_18, in_2, in_4);
  nor NOT_2 (out_20, in_6, in_6);
  nor OR_4 (OR_4_out, in_8, in_10);
  nor AND_3 (AND_3_out, in_11, in_13);
  nor AND_4 (AND_4_out, in_15, in_16);
  nor OR_5 (out_22, OR_4_out, OR_4_out);
  nor AND_5 (out_24, AND_3_out, AND_4_out);
endmodule

module PART3 (
  input  A1,
  input  A0,
  input  B1,
  input  B0,
  output C1,
  output C0
);

  wire AND_2_out, AND_3_out, AND_4_out, AND_out, NOT_2_out, NOT_out, OR_2_out, OR_out;

  nand NOT (NOT_out, A1, A1);
  nand NOT_2 (NOT_2_out, B1, B1);
  nand OR (OR_out, A1, A1);
  nand OR_2 (OR_2_out, B1, B1);
  nand AND (AND_out, NOT_out, B0);
  nand AND_2 (AND_2_out, B1, B0);
  nand AND_3 (AND_3_out, A0, NOT_2_out);
  nand AND_4 (AND_4_out, A1, A0);
  nand OR_3 (C1, OR_out, OR_2_out);
  nand OR_4 (C0, AND_out, AND_2_out, AND_3_out, AND_4_out);

  // Notes on the sheet:
  //   A1'
  //   B1'
  //   A1'B0
  //   A1A0
  //   A1'
  //   B1'
  //   B1B0
  //   A0B1'
  //   A1+B1
  //   A1'B0+B1B0+A0B1'+A1A0
endmodule

module PART4 (
  input  AI,
  input  BI,
  input  A,
  input  B,
  output O,
  output BO,
  output AO
);

  wire and_1_out, and_2_out, and_3_out, and_4_out, and_5_out, and_6_out, not_1_out, not_2_out, not_3_out,
       not_4_out, not_5_out, not_6_out, not_7_out, not_8_out;

  not not_1 (not_1_out, AI);
  not not_2 (not_2_out, BI);
  not not_3 (not_3_out, AI);
  not not_4 (not_4_out, A);
  not not_5 (not_5_out, AI);
  not not_6 (not_6_out, BI);
  not not_7 (not_7_out, B);
  not not_8 (not_8_out, BI);
  and and_1 (and_1_out, not_1_out, B);
  and and_2 (and_2_out, not_2_out, A);
  and and_3 (and_3_out, not_3_out, not_4_out, B);
  and and_4 (and_4_out, not_5_out, BI);
  and and_5 (and_5_out, not_6_out, A, not_7_out);
  and and_6 (and_6_out, AI, not_8_out);
  or or_1 (O, and_1_out, and_2_out);
  or or_2 (BO, and_3_out, and_4_out);
  or or_3 (AO, and_5_out, and_6_out);

  // Notes on the sheet:
  //   AI'B
  //   BI'A
  //   AI'A'B
  //   AI'BI
  //   BI'A'B'
  //   AIBI'
  //   AI'B+BI'A
  //   AI'A'B+AI'BI
  //   BI'AB'+AIBI'
endmodule

module PART5 (
  input  A0,
  input  B0,
  input  A1,
  input  B1,
  input  A2,
  input  B2,
  input  A3,
  input  B3,
  input  A0_2,
  input  B0_2,
  input  A1_2,
  input  B1_2,
  input  A2_2,
  input  B2_2,
  input  A3_2,
  input  B3_2,
  output O0,
  output O1,
  output O2,
  output O3,
  output O0_2,
  output O1_2,
  output O2_2,
  output O3_2
);

  wire altpart4_1_ao, altpart4_1_bo, altpart4_2_ao, altpart4_2_bo, altpart4_3_ao, altpart4_3_bo, part4_1_ao,
       part4_1_bo, part4_2_ao, part4_2_bo, part4_3_ao, part4_3_bo;

  PART4 part4_1 (.AI(1'b0), .O(O0), .BI(1'b0), .A(A0), .BO(part4_1_bo), .B(B0), .AO(part4_1_ao));
  altPART4 altpart4_1 (.B(B0_2), .A(A0_2), .BI(1'b0), .AI(1'b0), .O(O0_2), .BO(altpart4_1_bo), .AO(altpart4_1_ao));
  PART4 part4_2 (.AI(part4_1_ao), .O(O1), .BI(part4_1_bo), .A(A1), .BO(part4_2_bo), .B(B1), .AO(part4_2_ao));
  PART4 part4_3 (.AI(part4_2_ao), .O(O2), .BI(part4_2_bo), .A(A2), .BO(part4_3_bo), .B(B2), .AO(part4_3_ao));
  altPART4 altpart4_2 (
    .B(B1_2), .A(A1_2), .BI(altpart4_1_bo), .AI(altpart4_1_ao), .O(O1_2), .BO(altpart4_2_bo),
    .AO(altpart4_2_ao));
  altPART4 altpart4_3 (
    .B(B2_2), .A(A2_2), .BI(altpart4_2_bo), .AI(altpart4_2_ao), .O(O2_2), .BO(altpart4_3_bo),
    .AO(altpart4_3_ao));
  PART4 part4_4 (.AI(part4_3_ao), .O(O3), .BI(part4_3_bo), .A(A3), .B(B3));  // open: BO, AO
  altPART4 altpart4_4 (.B(B3_2), .A(A3_2), .BI(altpart4_3_bo), .AI(altpart4_3_ao), .O(O3_2));  // open: BO, AO
endmodule

module altPART4 (
  input  B,
  input  A,
  input  BI,
  input  AI,
  output O,
  output BO,
  output AO
);

  Multiplexer #(.select(4), .enable("false")) multiplexer_1 (
    .in0(1'b0), .in1(1'b1), .in2(1'b1), .in3(1'b1), .in4(1'b0), .in5(1'b1), .in6(1'b0), .in7(1'b1),
    .in8(1'b0), .in9(1'b0), .in10(1'b1), .in11(1'b1), .in12(1'b0), .in13(1'b0), .in14(1'b0), .in15(1'b0),
    .out(O), .sel({AI, BI, A, B}));
  Multiplexer #(.select(4), .enable("false")) multiplexer_2 (
    .in0(1'b0), .in1(1'b1), .in2(1'b0), .in3(1'b0), .in4(1'b1), .in5(1'b1), .in6(1'b1), .in7(1'b1),
    .in8(1'b0), .in9(1'b0), .in10(1'b0), .in11(1'b0), .in12(1'b0), .in13(1'b0), .in14(1'b0), .in15(1'b0),
    .out(BO), .sel({AI, BI, A, B}));
  Multiplexer #(.select(4), .enable("false")) multiplexer_3 (
    .in0(1'b0), .in1(1'b0), .in2(1'b1), .in3(1'b0), .in4(1'b0), .in5(1'b0), .in6(1'b0), .in7(1'b0),
    .in8(1'b1), .in9(1'b1), .in10(1'b1), .in11(1'b1), .in12(1'b0), .in13(1'b0), .in14(1'b0), .in15(1'b0),
    .out(AO), .sel({AI, BI, A, B}));
endmodule
