// Logisim project Lab06.circ as structural Verilog: 1 circuit, main circuit main
module main (
  input  A,
  input  En,
  input  B,
  output D,
  output V
);

  wire and_1_out, and_2_out, and_3_out, and_4_out, and_5_out, CLK_out, not_1_out, not_2_out, or_1_out,
       or_2_out, Q1_qn;

  Clock CLK (.out(CLK_out));
  D_Flip_Flop Q0 (.clk(CLK_out), .D(or_1_out), .Q(D));  // open: Qn, preset, en, reset
  D_Flip_Flop Q1 (.clk(CLK_out), .D(or_2_out), .Q(V), .Qn(Q1_qn));  // open: preset, en, reset
  not not_1 (not_1_out, A);
  not not_2 (not_2_out, B);
  and and_1 (and_1_out, A, Q1_qn, B, En);
  and and_2 (and_2_out, D, B, En);
  and and_3 (and_3_out, D, V, En);
  and and_4 (and_4_out, not_2_out, D, A, En);
  and and_5 (and_5_out, not_1_out, D, B, En);
  or or_1 (or_1_out, and_1_out, and_2_out, and_3_out);
  or or_2 (or_2_out, V, and_4_out, and_5_out);

  // Notes on the sheet:
  //   Q0B
  //   Q0B'A
  //   Q1'AB
  //   Q0Q1
  //   Q1
  //   Q0A'B
  //   EQ1'AB+EQ0AB'+EQ1
  //   EQ0A'B+EQ0AB'EQ1
endmodule
