// Logisim project Lab09 (1).circ as structural Verilog: 3 circuits, main circuit prototype
module prototype (
  input  CD,
  input  R
);

  wire CLK_out, data_1__3, data_1__16;
  wire [2:0] data_1_f, data_1_h;
  wire [5:0] control_1_hf;

  Clock CLK (.out(CLK_out));
  CONTROL control_1 (.H(data_1_h), .F(data_1_f), ._16(data_1__16), ._3(data_1__3), .CD(CD), .R(R), .HF(control_1_hf));
  DATA data_1 (
    .R(R), .CLK(CLK_out), .H(data_1_h), .F(data_1_f), ._16(data_1__16), ._3(data_1__3), .HF(control_1_hf),
    .CD(CD));
  LED HR (.in(data_1_h[0]));
  LED HY (.in(data_1_h[1]));
  LED HG (.in(data_1_h[2]));
  LED FR (.in(data_1_f[0]));
  LED FY (.in(data_1_f[1]));
  LED FG (.in(data_1_f[2]));
endmodule

module DATA (
  input  [5:0] HF,
  input  R,
  input  CD,
  input  CLK,
  output [2:0] H,
  output [2:0] F,
  output _16,
  output _3
);

  wire and_2_out, and_3_out, and_4_out, and_5_out, and_6_out, or_1_out, or_2_out, or_3_out, or_4_out, Q2_q;
  wire [1:0] _3_q;
  wire [3:0] _16_q;

  and and_1 (_3, _3_q[0], _3_q[1]);
  or or_1 (or_1_out, HF[5], ~or_2_out, HF[2]);  // OR_Gate
  or or_2 (or_2_out, HF[1], HF[4]);
  Counter #(.width(2), .max('h3)) u__3 (.count(or_2_out), .Q(_3_q), .clk(CLK), .clr(or_3_out));  // open: load, D, carry
  D_Flip_Flop Q2 (.clk(CLK), .D(_3), .Q(Q2_q));  // open: Qn, preset, en, reset
  Counter #(.width(4), .max('hf), .ongoal("stay")) u__16 (
    .count(or_1_out), .Q(_16_q), .clk(CLK), .clr(or_4_out));  // open: load, D, carry
  or or_3 (or_3_out, R, and_2_out);
  and and_2 (and_2_out, Q2_q, _3);
  and and_3 (and_3_out, and_6_out, CD);
  or or_4 (or_4_out, and_3_out, and_4_out, R);
  and and_4 (and_4_out, HF[1], _3, HF[3]);
  Register #(.width(3)) Q0 (.D(HF[5:3]), .Q(H), .clk(CLK), .clr(R));  // open: en
  Register #(.width(3)) Q1 (.D(HF[2:0]), .Q(F), .clk(CLK), .clr(R));  // open: en
  and and_5 (and_5_out, _16_q[0], _16_q[1], _16_q[2], _16_q[3]);
  D_Flip_Flop Q3 (.clk(CLK), .D(and_5_out), .Q(_16));  // open: Qn, preset, en, reset
  and and_6 (and_6_out, _16, and_5_out);

  // Notes on the sheet:
  //   splitter to only accept 3
  //   FY+HY
  //   HG+FG
  //   FY+HY
  //   HG+FG
  //   (Q3*16*CD)+(3*FY*HR)+R
  //   R+3*Q2
  //   3*Q2
  //   3*FY*HR
  //   Splitter accepts 16
  //   Q3*16*CD
  //   Q3*16
  //   Im sure the resets could be simplified down but this was the only way i could get it to work
endmodule

module CONTROL (
  input  [2:0] H,
  input  [2:0] F,
  input  _16,
  input  _3,
  input  CD,
  input  R,
  output [5:0] HF
);

  wire [1:0] rom_1_data;

  ROM #(.addrWidth(6), .dataWidth(2)) rom_1 (.addr({F, H}), .data(rom_1_data));  // open: sel
  ROM #(.addrWidth(6), .dataWidth(6)) rom_2 (.addr({R, CD, _3, _16, rom_1_data}), .data(HF));  // open: sel

  // Notes on the sheet:
  //   sets a 2 bit code to represent the current light combo
  //   contents of rom_1 (hex, n*v repeats v):
  //   10*0 1 6*0 3 15*0 2
  //   outputs the next lighting stage based on the conditions of the past light combo, 16 ticks, 3 ticks, Cd, and R
  //   contents of rom_2 (hex, n*v repeats v):
  //   21 11 c a 21 21 a a 21 c 7*21 11 c a 11 11 a 21 21 c c 21 21 21 a 33*21
  //   outputs a 6 bit code for the two lights
endmodule
