// Logisim project lab7.circ as structural Verilog: 1 circuit, main circuit main
module main (
  input  In,
  output Unlock
);

  wire and_1_out, and_2_out, and_3_out, and_5_out, clock_1_out, not_1_out, or_1_out, or_2_out, Q0_q, Q0_qn,
       Q1_q, Q1_qn, Q2_q, xor_1_out;

  Clock clock_1 (.out(clock_1_out));
  not not_1 (not_1_out, In);
  D_Flip_Flop Q0 (.clk(clock_1_out), .D(In), .Q(Q0_q), .Qn(Q0_qn));  // open: preset, en, reset
  D_Flip_Flop Q1 (.clk(clock_1_out), .D(or_1_out), .Q(Q1_q), .Qn(Q1_qn));  // open: preset, en, reset
  D_Flip_Flop Q2 (.clk(clock_1_out), .D(or_2_out), .Q(Q2_q));  // open: Qn, preset, en, reset
  xor xor_1 (xor_1_out, Q0_q, Q2_q);
  and and_1 (and_1_out, In, Q0_qn, Q1_qn, Q2_q);
  and and_2 (and_2_out, Q0_q, not_1_out);
  and and_3 (and_3_out, Q1_q, Q0_qn);
  and and_4 (Unlock, xor_1_out, Q1_q);
  or or_1 (or_1_out, and_1_out, and_2_out);
  and and_5 (and_5_out, and_2_out, Q2_q);
  or or_2 (or_2_out, and_5_out, and_3_out);
endmodule
